# Fritzing sketch circuit1blocard (saved by Fritzing 0.9.10b)
breadboards: 1

parts:
  Componente1 = Arduino Uno (Rev3) - ICSP
  S1 = Pushbutton [package="[THT]"]
  R1 = Resistor [tolerance=±5% power=0.25 resistance=220 package=THT]
  LED1 = smd LED [color="Red (633nm)" package="0805 [SMD]"]
  R2 = Resistor [tolerance=±5% resistance=220 package="2010 [SMD]"]

nets:
  N1: Componente1.GND, R1.Pin_1, LED1.anode
  N2: Componente1.D13/SCK, R2.Pin_0
  N3: Componente1.D2, S1.Pin_1, S1.Pin_2, R1.Pin_0
  N4: Componente1.5V, S1.Pin_3, S1.Pin_4
  N5: LED1.cathode, R2.Pin_1
