# Fritzing sketch circuit2blocard (saved by Fritzing 0.9.10b)
breadboards: 1

parts:
  Componente2 = Arduino Uno (Rev3) - ICSP
  LED2 = smd LED [color="Red (633nm)" package="0805 [SMD]"]
  R4 = Resistor [tolerance=±5% resistance=220 package="2010 [SMD]"]
  R5 = Rotary Potentiometer (Large) [maximum_resistance=100kΩ knob_status=50% power=0.5W package=THT]

nets:
  N1: Componente2.A5/SCL, R5.wiper
  N2: Componente2.ICSP_MOSI, Componente2.D11_PWM/MOSI, R4.Pin_0
  N3: Componente2.5V, R5.leg2
  N4: Componente2.GND, LED2.anode, R5.leg1
  N5: LED2.cathode, R4.Pin_1
