# Fritzing sketch circuit3blocard (saved by Fritzing 0.9.10b)
breadboards: 1

parts:
  Componente2 = Arduino Uno (Rev3) - ICSP
  R5 = Rotary Potentiometer (Large) [maximum_resistance=100kΩ knob_status=50% power=0.5W package=THT]
  M1 = DC Motor [voltage_(max)=6V voltage_(min)=3V]

nets:
  N1: Componente2.A5/SCL, R5.wiper
  N2: Componente2.D10_PWM/SS, M1.pin_1
  N3: Componente2.5V, R5.leg2
  N4: Componente2.GND, R5.leg1, M1.pin_2
