# Fritzing sketch circuit4blocard (saved by Fritzing 0.9.10b)
breadboards: 1

parts:
  Componente3 = Arduino Uno (Rev3) - ICSP
  R6 = Rotary Potentiometer (Large) [maximum_resistance=100kΩ knob_status=50% power=0.5W package=THT]
  R7 = Resistor [tolerance=±5% power=0.25 resistance=220 package=THT]
  LED1 = LED - 5mm [color="White (6500K)" current=0.030 package="5 mm [THT]"]
  R8 = Resistor [tolerance=±5% power=0.25 resistance=220 package=THT]
  R9 = Resistor [tolerance=±5% power=0.25 resistance=220 package=THT]
  R10 = Resistor [tolerance=±5% power=0.25 resistance=220 package=THT]
  R11 = Resistor [tolerance=±5% power=0.25 resistance=220 package=THT]
  LED2 = LED - 5mm [color="Yellow (592nm)" current=0.030 package="5 mm [THT]"]
  LED4 = LED - 5mm [color="Green (570nm)" current=0.030 package="5 mm [THT]"]
  LED5 = LED - 5mm [color="Blue (470nm)" current=0.030 package="5 mm [THT]"]
  LED3 = LED - 5mm [color="Red (635nm)" current=0.030 package="5 mm [THT]"]
  LED6 = LED - 3mm [color="White (4500K)" current=0.030 package="3 mm [THT]"]
  R12 = Resistor [tolerance=±5% power=0.25 resistance=220 package=THT]

nets:
  N1: Componente3.A5/SCL, R6.wiper
  N2: Componente3.ICSP_MISO, Componente3.D12/MISO, R10.Pin_1
  N3: Componente3.ICSP_MOSI, Componente3.D11_PWM/MOSI, R7.Pin_1
  N4: Componente3.D13/SCK, R8.Pin_1
  N5: Componente3.D1/TX, R12.Pin_1
  N6: Componente3.D2, R11.Pin_1
  N7: Componente3.D3_PWM, R9.Pin_1
  N8: Componente3.5V, R6.leg2
  N9: Componente3.GND, R6.leg1, LED1.anode, LED2.anode, LED4.anode, LED5.anode, LED3.anode, LED6.anode
  N10: R7.Pin_0, LED6.cathode
  N11: LED1.cathode, R8.Pin_0
  N12: R9.Pin_0, LED2.cathode
  N13: R10.Pin_0, LED3.cathode
  N14: R11.Pin_0, LED4.cathode
  N15: LED5.cathode, R12.Pin_0
