# Fritzing sketch presencia (saved by Fritzing 0.9.10b)
breadboards: 1

parts:
  Componente1 = Arduino Uno (Rev3) - ICSP
  M1 = fc-51 [package=THT]
  M2 = fc-51 [package=THT]

nets:
  N1: Componente1.GND, M1.pin3, M2.pin3
  N2: Componente1.D2, M2.pin1
  N3: Componente1.D3_PWM, M1.pin1
  N4: Componente1.5V, M1.pin2, M2.pin2
