# Fritzing sketch p3 (saved by Fritzing 0.9.10b)
breadboards: 1

parts:
  R1 = Photocell (LDR) [package=THT]
  R3 = Trimmer Potentiometer [maximum_resistance=10kΩ knob_status=50% power=0.5W package=THT]
  Componente1 = Arduino Uno (Rev3) - ICSP
  LED1 = LEDs [package=led10mm]
  R4 = Resistor [tolerance=±5% power=0.25 resistance=220 package=THT]

nets:
  N1: R1.pin_0, R3.wiper, Componente1.A5/SCL
  N2: R1.pin_1, Componente1.GND, LED1.C
  N3: R3.leg1, Componente1.5V
  N4: Componente1.D13/SCK, R4.Pin_1
  N5: LED1.A, R4.Pin_0
